# Fritzing sketch Water_Dispenser_Vendo (saved by Fritzing 0.9.3b)
breadboards: 2

parts:
  U1 = ESP32S-HiLetgo [part_number=ESP32S-HiLetgo]
  Part1 = Coin Acceptor - 6-Coin version
  A1 = Bill acceptor TB74-U
  HLK-PM1 = HLK-PM12 [part_number=HLK-PM12]
  M1 = RioRand LM2596
  J1 = Piezo Speaker
  M2 = RioRand LM2596
  U2 = ESP32S-HiLetgo [part_number=ESP32S-HiLetgo]
  RY1 = SSR-40VA
  RY3 = SSR-40VA
  A2 = Arduino pluggable terminal
  A3 = Arduino pluggable terminal
  DS1 = DS18B20 1-Wire Temperature Sensor [part_number=DS18B20]
  DS2 = DS18B20 1-Wire Temperature Sensor [part_number=DS18B20]
  A6 = yf-s401 flow sensor [package=THT]
  A7 = yf-s401 flow sensor [package=THT]
  Raspberry_Pi_1 = Raspberry Pi 4 [part_number=RPI-4-b]  # not connected
  M3 = 1 chan 5v relay module
  M4 = 1 chan 5v relay module
  M5 = 1 chan 5v relay module
  VALVE2 = Plastic Solenoid Valve
  VALVE3 = Plastic Solenoid Valve
  M6 = AC-05-03  # not connected
  A8 = 100w-ptc-air-heater
  J2 = Peltier Element
  VALVE1 = Plastic Solenoid Valve
  WATER_PUMP1 = water pump/motor
  WATER_PUMP2 = water pump/motor

nets:
  N1: U1.GPIO25, J1.pin2
  N2: U1.GPIO26, Part1.SIG
  GND: U1.GND, Part1.GND, A1.Pin_1, A1.Pin_2, A1.Pin_3, A1.Pin_4, HLK-PM1.-Vo, M1.Pin_2, M1.Pin_4, J1.pin1, M2.Pin_4, U2.GND, RY1.Pin_4, RY3.Pin_4, A2.Pin_3, A2.Pin_4, A3.Pin_3, A3.Pin_4, DS1.GND, DS2.GND, A6.pin2, A7.pin2, M3.pin_2, M4.pin_2, M5.pin_2, VALVE2.no_name_yet#2, VALVE3.no_name_yet#2, VALVE1.no_name_yet#2, WATER_PUMP1.pin_1, WATER_PUMP2.pin_1
  VIN: U1.VIN, Part1.12V, M1.Pin_3
  N3: U1.GPIO19, A1.Pin_5
  N4: A1.Pin_6, HLK-PM1.+Vo, M1.Pin_1, M2.Pin_1, M3.pin_4, M4.pin_4
  N5: M2.Pin_2, M2.Pin_3, U2.VIN, M3.pin_1, M4.pin_1, M5.pin_1
  VDD: U2.3.3, A2.Pin_2, A2.Pin_5, A3.Pin_2, A3.Pin_5, DS1.VDD, DS2.VDD, A6.pin1
  N6: U2.GPIO34, A6.pin3
  N7: U2.GPIO35, A7.pin3
  N8: U2.GPIO32, RY1.Pin_3
  N9: U2.GPIO25, RY3.Pin_3
  N10: U2.GPIO5, M5.pin_3
  N11: U2.GPIO18, M4.pin_3
  N12: U2.GPIO19, M3.pin_3
  N13: U2.GPIO22, A3.Pin_1, A3.Pin_6, DS2.DQ
  N14: U2.GPIO23, A2.Pin_1, A2.Pin_6, DS1.DQ
  N15: RY1.Pin_2, A8.Pin_2
  N16: RY3.Pin_2, J2.pin2
  N17: M3.pin_5, VALVE3.no_name_yet#1, WATER_PUMP1.pin_2
  N18: M4.pin_5, VALVE2.no_name_yet#1, WATER_PUMP2.pin_2
  N19: M5.pin_5, VALVE1.no_name_yet#1

custom parts:
  ESP32S-HiLetgo: HiLetgo ESP-WROOM-32 ESP32 ESP-32S Development Board 2.4GHz Dual-Mode WiFi + Bluetooth Dual Cores Microcontroller The ESP32 integrated with Antenna switches, RF Balun, power amplifiers, low-noise amplifiers, filters, and management modules, and the entire solution occupies the least area of PCB. 2.4 GHz Wi-Fi plus Bluetooth dual-mode chip, with TSMC Ultra-low power consumption 40nm technology,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
  Coin Acceptor - 6-Coin version: 12V coin acceptor that can handle up to 6 different denominations. Output is either pulse width, serial, or single pin per coin value.
  Bill acceptor TB74-U: The TB-Series is the latest generation of banknote reader designed exclusively by TOPVME with the highest safety and acceptance rate have over 96%.
  SSR-40VA: SSR-40VA solid state relay.
  Arduino pluggable terminal: Arduino pluggable terminal.
  yf-s401 flow sensor: Flow sensors sit in line with your water line, and uses a pinwheel sensor to measure how much liquid has moved through it.
  Raspberry Pi 4: The RPi4, a faster version of the awesome Raspberry Pi 2 B ARM Board with 40 pin gpio. Ready for special Raspberry Pi B+ and RPi2 Hat (Hardware attached (on) top)
  1 chan 5v relay module: 1 Channel 5V Relay Module Board Shield with Optocoupler Support High and Low Level Trigger for Arduino.
  AC-05-03: AC-DC 220V to 5V Step-Down Power Supply Module
  100w-ptc-air-heater: 110V 100W Surface Insulated PTC Air Heater PTC Heating Element Incubator Controller Incubation Heater.
  water pump/motor: WATER PUMP BY ARDUBLOCKTR
